// Digital circuit Filtre.dig as structural Verilog
module Filtre (
  input  [31:0] A,
  input  [31:0] B,
  input  [31:0] C,
  input  [31:0] D,
  input  Reset_registre,
  input  Clk,
  input  [32:0] AUDIO,
  input  rst_automate,
  output [15:0] S
);

  wire add_2_c_o, add_3_c_o, add_4_c_o, en_1, en_2, en_3, en_4, en_5, en_6, en_7, en_8;
  wire [2:0] s_mux;
  wire [7:0] add_1_s, reg8_1_q;
  wire [7:1] undriven;
  wire [15:0] add_6_s;
  wire [31:0] multiplexer_1_out, multiplexer_2_out, multiplexer_3_out, multiplexer_4_out, multiplexer_5_out,
       reg32_1_q, reg32_2_q, reg32_3_q, reg32_4_q, reg32_5_q, reg32_6_q, reg32_7_q, reg32_8_q, reg32_9_q,
       reg32_10_q, reg32_11_q, reg32_12_q, reg32_13_q, reg32_14_q, reg32_15_q, reg32_16_q, reg32_17_q,
       reg32_18_q, reg32_19_q, reg32_20_q, reg32_21_q, reg32_22_q, reg32_23_q, reg32_24_q, reg32_25_q,
       reg32_26_q, reg32_27_q, reg32_28_q, reg32_29_q, reg32_30_q, reg32_31_q, reg32_32_q;
  wire [32:0] add_2_s, add_3_s, add_4_s, add_5_s;
  wire [63:0] mul_1_mul, mul_2_mul, mul_3_mul, mul_4_mul;

  Reg8 reg8_1 (.EN(1'b1), .Reset(rst_automate), .CLK(Clk), .D(add_1_s), .Q(reg8_1_q));
  Add #(.Bits(8)) add_1 (.a(reg8_1_q), .b({undriven, 1'b1}), .c_i(1'b0), .s(add_1_s));  // open: c_o
  LookUpTable #(.Bits(11)) \table  (
    .in0(add_1_s[0]), .in1(add_1_s[1]), .in2(add_1_s[2]), .in3(add_1_s[3]), .in4(add_1_s[4]),
    .in5(add_1_s[5]), .in6(add_1_s[6]), .in7(add_1_s[7]),
    .out({s_mux, en_8, en_7, en_6, en_5, en_4, en_3, en_2, en_1}));
  Reg32 reg32_1 (.D(AUDIO[31:0]), .Clk(Clk), .Reset(Reset_registre), .Enable(en_8), .Q(reg32_1_q));
  Reg32 reg32_2 (.D(AUDIO[31:0]), .Clk(Clk), .Reset(Reset_registre), .Enable(en_7), .Q(reg32_2_q));
  Reg32 reg32_3 (.D(AUDIO[31:0]), .Clk(Clk), .Reset(Reset_registre), .Enable(en_6), .Q(reg32_3_q));
  Reg32 reg32_4 (.D(AUDIO[31:0]), .Clk(Clk), .Reset(Reset_registre), .Enable(en_5), .Q(reg32_4_q));
  Reg32 reg32_5 (.D(AUDIO[31:0]), .Clk(Clk), .Reset(Reset_registre), .Enable(en_4), .Q(reg32_5_q));
  Reg32 reg32_6 (.D(AUDIO[31:0]), .Clk(Clk), .Reset(Reset_registre), .Enable(en_3), .Q(reg32_6_q));
  Reg32 reg32_7 (.D(AUDIO[31:0]), .Clk(Clk), .Reset(Reset_registre), .Enable(en_2), .Q(reg32_7_q));
  Reg32 reg32_8 (.D(AUDIO[31:0]), .Clk(Clk), .Reset(Reset_registre), .Enable(en_1), .Q(reg32_8_q));
  Mul #(.Signed("true"), .Bits(32)) mul_1 (.a(multiplexer_1_out), .b(A), .mul(mul_1_mul));
  Add #(.Bits(33)) add_2 (.a(mul_1_mul[32:0]), .b(AUDIO), .c_i(1'b0), .s(add_2_s), .c_o(add_2_c_o));
  Multiplexer #(.Selector_Bits(3), .Bits(32)) multiplexer_1 (
    .sel(s_mux), .in_0(reg32_8_q), .in_1(reg32_7_q), .in_2(reg32_6_q), .in_3(reg32_5_q), .in_4(reg32_4_q),
    .in_5(reg32_3_q), .in_6(reg32_2_q), .in_7(reg32_1_q), .out(multiplexer_1_out));
  Reg32 reg32_9 (.D(reg32_1_q), .Clk(Clk), .Reset(Reset_registre), .Enable(en_8), .Q(reg32_9_q));
  Reg32 reg32_10 (.D(reg32_2_q), .Clk(Clk), .Reset(Reset_registre), .Enable(en_7), .Q(reg32_10_q));
  Reg32 reg32_11 (.D(reg32_3_q), .Clk(Clk), .Reset(Reset_registre), .Enable(en_6), .Q(reg32_11_q));
  Reg32 reg32_12 (.D(reg32_4_q), .Clk(Clk), .Reset(Reset_registre), .Enable(en_5), .Q(reg32_12_q));
  Reg32 reg32_13 (.D(reg32_5_q), .Clk(Clk), .Reset(Reset_registre), .Enable(en_4), .Q(reg32_13_q));
  Reg32 reg32_14 (.D(reg32_6_q), .Clk(Clk), .Reset(Reset_registre), .Enable(en_3), .Q(reg32_14_q));
  Reg32 reg32_15 (.D(reg32_7_q), .Clk(Clk), .Reset(Reset_registre), .Enable(en_2), .Q(reg32_15_q));
  Reg32 reg32_16 (.D(reg32_8_q), .Clk(Clk), .Reset(Reset_registre), .Enable(en_1), .Q(reg32_16_q));
  Mul #(.Signed("true"), .Bits(32)) mul_2 (.a(multiplexer_2_out), .b(B), .mul(mul_2_mul));
  Add #(.Bits(33)) add_3 (.a(mul_2_mul[32:0]), .b(add_2_s), .c_i(add_2_c_o), .s(add_3_s), .c_o(add_3_c_o));
  Multiplexer #(.Selector_Bits(3), .Bits(32)) multiplexer_2 (
    .sel(s_mux), .in_0(reg32_16_q), .in_1(reg32_15_q), .in_2(reg32_14_q), .in_3(reg32_13_q),
    .in_4(reg32_12_q), .in_5(reg32_11_q), .in_6(reg32_10_q), .in_7(reg32_9_q), .out(multiplexer_2_out));
  Mul #(.Signed("true"), .Bits(32)) mul_3 (.a(multiplexer_3_out), .b(C), .mul(mul_3_mul));
  Add #(.Bits(33)) add_4 (.a(mul_3_mul[32:0]), .b(add_3_s), .c_i(add_3_c_o), .s(add_4_s), .c_o(add_4_c_o));
  Multiplexer #(.Selector_Bits(3), .Bits(32)) multiplexer_3 (
    .sel(s_mux), .in_0(reg32_24_q), .in_1(reg32_23_q), .in_2(reg32_22_q), .in_3(reg32_21_q),
    .in_4(reg32_20_q), .in_5(reg32_19_q), .in_6(reg32_18_q), .in_7(reg32_17_q), .out(multiplexer_3_out));
  Reg32 reg32_17 (.D(reg32_25_q), .Clk(Clk), .Reset(Reset_registre), .Enable(en_8), .Q(reg32_17_q));
  Reg32 reg32_18 (.D(reg32_26_q), .Clk(Clk), .Reset(Reset_registre), .Enable(en_7), .Q(reg32_18_q));
  Reg32 reg32_19 (.D(reg32_27_q), .Clk(Clk), .Reset(Reset_registre), .Enable(en_6), .Q(reg32_19_q));
  Reg32 reg32_20 (.D(reg32_28_q), .Clk(Clk), .Reset(Reset_registre), .Enable(en_5), .Q(reg32_20_q));
  Reg32 reg32_21 (.D(reg32_29_q), .Clk(Clk), .Reset(Reset_registre), .Enable(en_4), .Q(reg32_21_q));
  Reg32 reg32_22 (.D(reg32_30_q), .Clk(Clk), .Reset(Reset_registre), .Enable(en_3), .Q(reg32_22_q));
  Reg32 reg32_23 (.D(reg32_31_q), .Clk(Clk), .Reset(Reset_registre), .Enable(en_2), .Q(reg32_23_q));
  Reg32 reg32_24 (.D(reg32_32_q), .Clk(Clk), .Reset(Reset_registre), .Enable(en_1), .Q(reg32_24_q));
  Add #(.Bits(33)) add_5 (.a(mul_4_mul[32:0]), .b(add_4_s), .c_i(add_4_c_o), .s(add_5_s));  // open: c_o
  Mul #(.Signed("true"), .Bits(32)) mul_4 (.a(multiplexer_4_out), .b(D), .mul(mul_4_mul));
  Multiplexer #(.Selector_Bits(3), .Bits(32)) multiplexer_4 (
    .sel(s_mux), .in_0(reg32_32_q), .in_1(reg32_31_q), .in_2(reg32_30_q), .in_3(reg32_29_q),
    .in_4(reg32_28_q), .in_5(reg32_27_q), .in_6(reg32_26_q), .in_7(reg32_25_q), .out(multiplexer_4_out));
  Reg32 reg32_25 (.D(add_5_s[31:0]), .Clk(Clk), .Reset(Reset_registre), .Enable(en_8), .Q(reg32_25_q));
  Reg32 reg32_26 (.D(add_5_s[31:0]), .Clk(Clk), .Reset(Reset_registre), .Enable(en_7), .Q(reg32_26_q));
  Reg32 reg32_27 (.D(add_5_s[31:0]), .Clk(Clk), .Reset(Reset_registre), .Enable(en_6), .Q(reg32_27_q));
  Reg32 reg32_28 (.D(add_5_s[31:0]), .Clk(Clk), .Reset(Reset_registre), .Enable(en_5), .Q(reg32_28_q));
  Reg32 reg32_29 (.D(add_5_s[31:0]), .Clk(Clk), .Reset(Reset_registre), .Enable(en_4), .Q(reg32_29_q));
  Reg32 reg32_30 (.D(add_5_s[31:0]), .Clk(Clk), .Reset(Reset_registre), .Enable(en_3), .Q(reg32_30_q));
  Reg32 reg32_31 (.D(add_5_s[31:0]), .Clk(Clk), .Reset(Reset_registre), .Enable(en_2), .Q(reg32_31_q));
  Reg32 reg32_32 (.D(add_5_s[31:0]), .Clk(Clk), .Reset(Reset_registre), .Enable(en_1), .Q(reg32_32_q));
  Multiplexer #(.Bits(32)) multiplexer_5 (
    .sel(add_5_s[31]), .in_0(32'h8000), .in_1(32'hffff8000), .out(multiplexer_5_out));
  Add #(.Bits(32)) add_6 (.a(add_5_s[31:0]), .b(multiplexer_5_out), .c_i(1'b0), .s({S, add_6_s}));  // open: c_o
  // Pins of 32 and 33 bits meet at AUDIO
  // Pins of 32 and 33 bits meet at add_5_s
  // Pins of 33 and 64 bits meet at mul_1_mul
  // Pins of 33 and 64 bits meet at mul_2_mul
  // Pins of 33 and 64 bits meet at mul_3_mul
  // Pins of 33 and 64 bits meet at mul_4_mul
  // Pins of 1 and 8 bits meet at {undriven, 1'b1}

  // Other names for the same wires on the sheet: rst = Reset_registre
endmodule
