// Digital circuit Reg32.dig as structural Verilog
module Reg32 (
  input  [31:0] D,
  input  Clk,
  input  Reset,
  input  Enable,
  output [31:0] Q
);

  Reg8 reg8_1 (.EN(Enable), .Reset(Reset), .CLK(Clk), .D(D[7:0]), .Q(Q[7:0]));
  Reg8 reg8_2 (.EN(Enable), .Reset(Reset), .CLK(Clk), .D(D[15:8]), .Q(Q[15:8]));
  Reg8 reg8_3 (.EN(Enable), .Reset(Reset), .CLK(Clk), .D(D[23:16]), .Q(Q[23:16]));
  Reg8 reg8_4 (.EN(Enable), .Reset(Reset), .CLK(Clk), .D(D[31:24]), .Q(Q[31:24]));
endmodule
