// Digital circuit Reg8.dig as structural Verilog
module Reg8 (
  input  EN,
  input  Reset,
  input  CLK,
  input  [7:0] D,
  output [7:0] Q
);

  wire [7:0] multiplexer_1_out;

  Multiplexer #(.Bits(8)) multiplexer_1 (.sel(EN), .in_0(Q), .in_1(D), .out(multiplexer_1_out));
  D_FF_AS #(.Bits(8)) d_ff_as_1 (.Set(1'b0), .D(multiplexer_1_out), .C(CLK), .Clr(Reset), .Q(Q));  // open: nQ
endmodule
