// Digital circuit Reg_1bit.dig as structural Verilog
module Reg_1bit (
  input  EN,
  input  Reset,
  input  CLK,
  input  D,
  output Q
);

  wire multiplexer_1_out;

  Multiplexer multiplexer_1 (.sel(EN), .in_0(Q), .in_1(D), .out(multiplexer_1_out));
  D_FF_AS d_ff_as_1 (.Set(1'b0), .D(multiplexer_1_out), .C(CLK), .Clr(Reset), .Q(Q));  // open: nQ
endmodule
