// Digital circuit automate.dig as structural Verilog
module automate (
  input  rst_automate,
  input  Clk
);

  wire en_1, en_2, en_3, en_4, en_5, en_6, en_7, en_8;
  wire [2:0] s_mux;
  wire [7:0] add_1_s, reg8_1_q;
  wire [7:1] undriven;

  Reg8 reg8_1 (.EN(1'b1), .Reset(rst_automate), .CLK(Clk), .D(add_1_s), .Q(reg8_1_q));
  Add #(.Bits(8)) add_1 (.a(reg8_1_q), .b({undriven, 1'b1}), .c_i(1'b0), .s(add_1_s));  // open: c_o
  LookUpTable #(.Bits(11)) \table  (
    .in0(add_1_s[0]), .in1(add_1_s[1]), .in2(add_1_s[2]), .in3(add_1_s[3]), .in4(add_1_s[4]),
    .in5(add_1_s[5]), .in6(add_1_s[6]), .in7(add_1_s[7]),
    .out({s_mux, en_8, en_7, en_6, en_5, en_4, en_3, en_2, en_1}));
  // Pins of 1 and 8 bits meet at {undriven, 1'b1}
endmodule
