// Digital circuit reg_4bit.dig as structural Verilog
module reg_4bit (
  input  [3:0] D,
  input  Clk,
  input  Reset,
  input  Enable,
  output [3:0] Q
);

  Reg_1bit reg_1bit_1 (.EN(Enable), .Reset(Reset), .CLK(Clk), .D(D[0]), .Q(Q[0]));
  Reg_1bit reg_1bit_2 (.EN(Enable), .Reset(Reset), .CLK(Clk), .D(D[1]), .Q(Q[1]));
  Reg_1bit reg_1bit_3 (.EN(Enable), .Reset(Reset), .CLK(Clk), .D(D[2]), .Q(Q[2]));
  Reg_1bit reg_1bit_4 (.EN(Enable), .Reset(Reset), .CLK(Clk), .D(D[3]), .Q(Q[3]));
endmodule
