// Digital circuit table_test.dig as structural Verilog
module table_test (
  input  rst_automate,
  input  Clk,
  output [1:0] S
);

  wire [1:0] lookuptable_1_out;
  wire [3:0] add_1_s, reg_4bit_1_q;

  reg_4bit reg_4bit_1 (.D(add_1_s), .Clk(Clk), .Reset(rst_automate), .Enable(1'b1), .Q(reg_4bit_1_q));
  Add #(.Bits(4)) add_1 (.a(reg_4bit_1_q), .b(4'b0001), .c_i(1'b0), .s(add_1_s));  // open: c_o
  LookUpTable #(.Bits(2)) lookuptable_1 (
    .in0(reg_4bit_1_q[0]), .in1(reg_4bit_1_q[1]), .in2(reg_4bit_1_q[2]), .in3(reg_4bit_1_q[3]),
    .out(lookuptable_1_out));
  Multiplexer #(.Selector_Bits(2), .Bits(2)) multiplexer_1 (
    .sel(lookuptable_1_out), .in_0(2'b00), .in_1(2'b01), .in_2(2'b10), .in_3(2'b11), .out(S));

  // Notes on the sheet:
  //   contents of lookuptable_1 (hex, n*v repeats v):
  //   0,1,2,3,0,1,2,3,0,1,2,3,0,1,2,3
endmodule
